// Logisim project evolution_D_FF.circ as structural Verilog
module sr_latch (
  input  preset,
  input  reset,
  input  enable,
  input  set,
  input  clear,
  output oout
);

  wire B_out, C_out, D_out, E_out, F_out, G_out, H_out, not_1_out, not_2_out;

  and H (H_out, enable, set);
  not not_1 (not_1_out, clear);
  and F (F_out, reset, enable);
  not not_2 (not_2_out, F_out);
  or G (G_out, H_out, oout);
  and B (B_out, not_1_out, D_out);
  or D (D_out, preset, not_2_out);
  or E (E_out, G_out, preset);
  and C (C_out, E_out, not_1_out);
  and and_1 (oout, B_out, C_out);
endmodule

module d_latch (
  input  preset,
  input  enable,
  input  data,
  input  clear,
  output Q
);

  wire not_1_out;

  not not_1 (not_1_out, data);
  sr_latch sr_latch_1 (.preset(preset), .reset(not_1_out), .enable(enable), .set(data), .clear(clear), .oout(Q));
endmodule

module d_flipflop (
  input  preset,
  input  clk,
  input  data,
  input  clear,
  output Q
);

  wire d_latch_1_q, not_1_out;

  not not_1 (not_1_out, clk);
  d_latch d_latch_1 (.preset(preset), .enable(not_1_out), .data(data), .clear(clear), .Q(d_latch_1_q));
  d_latch d_latch_2 (.preset(preset), .enable(clk), .data(d_latch_1_q), .clear(clear), .Q(Q));
endmodule
